// Logisim project 4_bit_binary_adder_subtractor.circ as structural Verilog: 1 circuit, main circuit main
// 4-Bit Binary Adder / Subtractor
module main (
  input  B0,
  input  A0,
  input  B1,
  input  A1,
  input  B2,
  input  A2,
  input  B3,
  input  A3,
  input  SUB,
  output S0,
  output S1,
  output S2,
  output S3,
  output Cout
);

  wire and_1_p3, and_2_p3, and_3_p3, and_4_p3, and_5_p3, and_6_p3, and_7_p3, and_8_p3, xor_5_p1, xor_6_p1,
       xor_7_p1, xor_8_p1, xor_9_p1, xor_10_p1, xor_10_p2, xor_11_p1, xor_11_p2, xor_12_p1, xor_12_p2;

  // XOR_Gate xor_1: pin names not known; wires that end beside it: B0, SUB
  // XOR_Gate xor_2: pin names not known; wires that end beside it: B1, SUB
  // XOR_Gate xor_3: pin names not known; wires that end beside it: B2, SUB
  // XOR_Gate xor_4: pin names not known; wires that end beside it: B3, SUB
  // XOR_Gate xor_5: pin names not known; wires that end beside it: xor_5_p1, A0
  // AND_Gate and_1: pin names not known; wires that end beside it: A0, xor_5_p1, and_1_p3
  // XOR_Gate xor_6: pin names not known; wires that end beside it: xor_6_p1, A1
  // AND_Gate and_2: pin names not known; wires that end beside it: A1, xor_6_p1, and_2_p3
  // XOR_Gate xor_7: pin names not known; wires that end beside it: xor_7_p1, A2
  // AND_Gate and_3: pin names not known; wires that end beside it: A2, xor_7_p1, and_3_p3
  // XOR_Gate xor_8: pin names not known; wires that end beside it: xor_8_p1, A3
  // AND_Gate and_4: pin names not known; wires that end beside it: A3, xor_8_p1, and_4_p3
  // XOR_Gate xor_9: pin names not known; wires that end beside it: xor_9_p1, SUB, S0
  // AND_Gate and_5: pin names not known; wires that end beside it: xor_9_p1, SUB, and_5_p3
  // XOR_Gate xor_10: pin names not known; wires that end beside it: xor_10_p1, xor_10_p2, S1
  // AND_Gate and_6: pin names not known; wires that end beside it: xor_10_p1, xor_10_p2, and_6_p3
  // XOR_Gate xor_11: pin names not known; wires that end beside it: xor_11_p1, xor_11_p2, S2
  // AND_Gate and_7: pin names not known; wires that end beside it: xor_11_p1, xor_11_p2, and_7_p3
  // XOR_Gate xor_12: pin names not known; wires that end beside it: xor_12_p1, xor_12_p2, S3
  // AND_Gate and_8: pin names not known; wires that end beside it: xor_12_p1, xor_12_p2, and_8_p3
  // OR_Gate or_1 has open pins: in0=and_1_p3, in1=and_5_p3, out=open
  // OR_Gate or_2 has open pins: in0=and_2_p3, in1=and_6_p3, out=open
  // OR_Gate or_3 has open pins: in0=and_3_p3, in1=and_7_p3, out=open
  // OR_Gate or_4 has open pins: in0=and_4_p3, in1=and_8_p3, out=open

  // Notes on the sheet:
  //   SUB=0: A+B    |    SUB=1: A-B
  //   B XOR SUB
  //   4-BIT BINARY ADDER / SUBTRACTOR
  //   Ripple-carry 2's-complement adder/subtractor
endmodule
